// Logisim project 4-bit-cpu-v2.circ as structural Verilog: 3 circuits, main circuit main
module main (
  input  in_1,
  input  in_2,
  input  in_3,
  input  in_4,
  input  RESET,
  input  in_6
);

  wire BREAK, clock_1_out, counter_2_carry, d_ff_1_q, decoder_1_out0, decoder_1_out1, decoder_1_out2,
       decoder_1_out3, decoder_2_out0, decoder_2_out1, decoder_2_out2, decoder_2_out3, LDPC, movz_1_bmx0,
       movz_1_bmx1, movz_1_brk, movz_1_raeo, movz_1_rwram, movz_1_ze, nop_1_bmx0, nop_1_bmx1, nop_1_brk,
       nop_1_ldpco, nop_1_raeo, nop_1_rwram, nop_1_ze, not_1_out, not_2_out, or_1_out, RAE, RWRAM, ZE;
  wire [1:0] BUS_MUX, counter_2_q;
  wire [3:0] counter_1_q, multiplexer_1_out, ram_1_data, register_1_q, register_2_q, register_3_q, rom_1_data;

  // Probe on LDPC
  not not_1 (not_1_out, LDPC);
  Clock clock_1 (.out(clock_1_out));
  Counter #(.width(4), .max('hf)) counter_1 (
    .load(LDPC), .D(multiplexer_1_out), .count(not_1_out), .Q(counter_1_q), .clk(clock_1_out), .clr(RESET));  // open: carry
  Register #(.width(4)) register_1 (.D(multiplexer_1_out), .en(RAE), .Q(register_1_q), .clk(clock_1_out));  // open: clr
  // Probe on RAE
  RAM #(.addrWidth(4), .dataWidth(4)) ram_1 (
    .addr(register_1_q), .data(ram_1_data), .clk(clock_1_out), .ld(not_2_out));  // open: sel, clr
  not not_2 (not_2_out, RWRAM);
  ROM #(.addrWidth(4), .dataWidth(4)) rom_1 (.addr(counter_1_q), .data(rom_1_data));  // open: sel
  assign ram_1_data = RWRAM ? multiplexer_1_out : 4'bz;  // Controlled_Buffer controlled_buffer_1
  // Probe on RWRAM
  Register #(.width(4)) register_2 (.D(multiplexer_1_out), .en(ZE), .Q(register_2_q), .clk(clock_1_out));  // open: clr
  // Probe on ZE
  Register #(.width(4)) register_3 (.D(rom_1_data), .en(or_1_out), .Q(register_3_q), .clk(clock_1_out));  // open: clr
  Multiplexer #(.select(2), .width(4)) multiplexer_1 (
    .in0(rom_1_data), .in1(ram_1_data), .in2(register_2_q), .out(multiplexer_1_out), .sel(BUS_MUX), .en(1'b1));  // open: in3
  // Probe on BUS_MUX
  Decoder #(.select(4)) decoder_1 (
    .out0(decoder_1_out0), .out1(decoder_1_out1), .out2(decoder_1_out2), .out3(decoder_1_out3),
    .sel(register_3_q));  // open: out4, out5, out6, out7, out8, out9, out10, out11, out12, out13, out14, out15, en
  Counter #(.width(2), .max('h3)) counter_2 (
    .Q(counter_2_q), .carry(counter_2_carry), .clk(clock_1_out), .clr(d_ff_1_q));  // open: load, D, count
  or or_1 (or_1_out, d_ff_1_q, decoder_1_out0, counter_2_carry);
  D_Flip_Flop d_ff_1 (.clk(clock_1_out), .D(BREAK), .Q(d_ff_1_q));  // open: Qn, preset, en, reset
  Decoder #(.select(2)) decoder_2 (
    .out0(decoder_2_out0), .out1(decoder_2_out1), .out2(decoder_2_out2), .out3(decoder_2_out3),
    .sel(counter_2_q));  // open: en
  NOP nop_1 (
    .CS0(decoder_2_out0), .CS1(decoder_2_out1), .CS2(decoder_2_out2), .CS3(decoder_2_out3),
    .ENABLE(decoder_1_out0), .LDPCO(nop_1_ldpco), .ZE(nop_1_ze), .RWRAM(nop_1_rwram), .RAEO(nop_1_raeo),
    .BMX0(nop_1_bmx0), .BMX1(nop_1_bmx1), .BRK(nop_1_brk));
  MOVZ movz_1 (
    .CS0(decoder_2_out0), .CS1(decoder_2_out1), .CS2(decoder_2_out2), .CS3(decoder_2_out3),
    .ENABLE(decoder_1_out1), .LDPCO(nop_1_bmx0), .ZE(movz_1_ze), .RWRAM(movz_1_rwram), .RAEO(movz_1_raeo),
    .BMX0(movz_1_bmx0), .BMX1(movz_1_bmx1), .BRK(movz_1_brk));
  or or_2 (LDPC, nop_1_ldpco, nop_1_bmx0);
  or or_3 (ZE, nop_1_ze, movz_1_ze);
  or or_4 (RWRAM, nop_1_rwram, movz_1_rwram);
  or or_5 (RAE, nop_1_raeo, movz_1_raeo);
  or or_6 (BUS_MUX[0], nop_1_bmx0, movz_1_bmx0);
  or or_7 (BUS_MUX[1], nop_1_bmx1, movz_1_bmx1);
  or or_8 (BREAK, nop_1_brk, in_6, movz_1_brk);

  // Notes on the sheet:
  //   LDPC
  //   RAM
  //   PROG MEM
  //   contents of rom_1 (hex, n*v repeats v):
  //   1 1 5 4 5 6 7 1 9 a b c d e f
  //   R/W RAM
  //   Z REG
  //   INSTRUCTION REG
  //   break cycle logic
  //   CPU CYCLE
endmodule

module NOP (
  input  CS0,
  input  CS1,
  input  CS2,
  input  CS3,
  input  ENABLE,
  output LDPCO,
  output ZE,
  output RWRAM,
  output RAEO,
  output BMX0,
  output BMX1,
  output BRK
);


  assign BMX0 = 1'b0;
  assign BMX1 = 1'b0;
  assign BRK = 1'b0;
  assign CS1 = CS0;
  assign CS2 = CS0;
  assign CS3 = CS0;
  assign ENABLE = CS0;
  assign LDPCO = 1'b0;
  assign RAEO = 1'b0;
  assign RWRAM = 1'b0;
  assign ZE = 1'b0;
  // also tied to GND on the sheet: CS0
endmodule

module MOVZ (
  input  CS0,
  input  CS1,
  input  CS2,
  input  CS3,
  input  ENABLE,
  output LDPCO,
  output ZE,
  output RWRAM,
  output RAEO,
  output BMX0,
  output BMX1,
  output BRK
);

  wire controlled_buffer_5_out, controlled_buffer_7_out, pull_resistor_1_node, pull_resistor_2_node;

  assign RAEO = pull_resistor_1_node ? pull_resistor_1_node : 1'bz;  // Controlled_Buffer controlled_buffer_1
  Pull_Resistor pull_resistor_1 (.node(pull_resistor_1_node));
  assign ZE = pull_resistor_2_node ? pull_resistor_2_node : 1'bz;  // Controlled_Buffer controlled_buffer_2
  assign pull_resistor_1_node = ENABLE ? CS0 : 1'bz;  // Controlled_Buffer controlled_buffer_3
  Pull_Resistor pull_resistor_2 (.node(pull_resistor_2_node));
  assign pull_resistor_2_node = ENABLE ? CS1 : 1'bz;  // Controlled_Buffer controlled_buffer_4
  assign controlled_buffer_5_out = ENABLE ? CS2 : 1'bz;  // Controlled_Buffer controlled_buffer_5
  assign BMX0 = controlled_buffer_5_out ? controlled_buffer_5_out : 1'bz;  // Controlled_Buffer controlled_buffer_6
  Pull_Resistor pull_resistor_3 (.node(controlled_buffer_5_out));
  assign controlled_buffer_7_out = ENABLE ? CS3 : 1'bz;  // Controlled_Buffer controlled_buffer_7
  assign BRK = controlled_buffer_7_out ? controlled_buffer_7_out : 1'bz;  // Controlled_Buffer controlled_buffer_8
  Pull_Resistor pull_resistor_4 (.node(controlled_buffer_7_out));
  Pull_Resistor pull_resistor_5 (.node(BMX1));
  Pull_Resistor pull_resistor_6 (.node(ZE));
  Pull_Resistor pull_resistor_7 (.node(RAEO));
  Pull_Resistor pull_resistor_8 (.node(BMX0));
  Pull_Resistor pull_resistor_9 (.node(BRK));

  assign LDPCO = BMX1;
  assign RWRAM = BMX1;

  // Notes on the sheet:
  //   INSUTRCTION EXECUTE STAGE
  //   CONTROL WORD
endmodule
